// Logisim project 2-4.circ as structural Verilog: 1 circuit, main circuit main
module main (
  input  bit_1,
  input  bit_2,
  output bit_4,
  output bit_3,
  output bit_2_2,
  output bit_1_2
);

  wire not_1_out, not_2_out, or_1_out, or_2_out, or_3_out;

  and and_1 (bit_4, bit_1, bit_2);
  not not_1 (not_1_out, bit_2);
  or or_1 (or_1_out, bit_1, not_1_out);
  not not_2 (not_2_out, bit_1);
  not not_3 (bit_3, or_1_out);
  or or_2 (or_2_out, not_2_out, bit_2);
  or or_3 (or_3_out, bit_1, bit_2);
  not not_4 (bit_2_2, or_2_out);
  not not_5 (bit_1_2, or_3_out);
endmodule
