// Logisim project 4-2.circ as structural Verilog: 1 circuit, main circuit main
module main (
  input  bit_1,
  input  bit_2,
  input  bit_3,
  input  bit_4,
  output bit_1_2,
  output bit_2_2
);

  or or_1 (bit_1_2, bit_4, bit_2);
  or or_2 (bit_2_2, bit_3, bit_4);
endmodule
