// Logisim project myFirst.circ as structural Verilog: 1 circuit, main circuit main
module main (
  input  in_1,
  output out_2
);

  wire nand_1_out, nor_1_out, not_1_out;

  not not_1 (not_1_out, in_1);
  nand nand_1 (nand_1_out, in_1, in_1);
  nor nor_1 (nor_1_out, not_1_out, in_1);
  xor xor_1 (out_2, nand_1_out, nor_1_out);
endmodule
