// Logisim project alu-1.circ as structural Verilog: 3 circuits, main circuit main
module main (
  input  CarryIn,
  input  Selector0,
  input  Selector1,
  input  Input0,
  input  Input1,
  output Output,
  output CarryOut
);

  wire and_1_out, fa_1_1_result, or_1_out;

  and and_1 (and_1_out, Input0, Input1);
  or or_1 (or_1_out, Input1, Input0);
  fa_1 fa_1_1 (.Input0(Input0), .Input1(Input1), .CarryIn(CarryIn), .Result(fa_1_1_result), .CarryOut(CarryOut));
  mux_4i mux_4i_1 (
    .Input0(and_1_out), .Input1(fa_1_1_result), .Input2(or_1_out), .S0(Selector0), .S1(Selector1),
    .Output(Output));  // open: Input3
endmodule

module mux_4i (
  input  S0,
  input  S1,
  input  Input0,
  input  Input1,
  input  Input2,
  input  Input3,
  output Output
);

  wire and_1_out, and_2_out, and_3_out, and_4_out, not_1_out, not_2_out, not_3_out, not_4_out;

  not not_1 (not_1_out, S0);
  not not_2 (not_2_out, S0);
  and and_1 (and_1_out, Input0, not_1_out, not_3_out);
  not not_3 (not_3_out, S1);
  and and_2 (and_2_out, Input1, not_2_out, S1);
  and and_3 (and_3_out, Input2, S0, not_4_out);
  not not_4 (not_4_out, S1);
  and and_4 (and_4_out, Input3, S0, S1);
  or or_1 (Output, and_1_out, and_2_out, and_3_out, and_4_out);
endmodule

module fa_1 (
  input  Input0,
  input  Input1,
  input  CarryIn,
  output Result,
  output CarryOut
);

  wire and_1_out, and_2_out, xor_1_out;

  xor xor_1 (xor_1_out, Input0, Input1);
  and and_1 (and_1_out, Input0, Input1);
  and and_2 (and_2_out, CarryIn, xor_1_out);
  xor xor_2 (Result, xor_1_out, CarryIn);
  or or_1 (CarryOut, and_2_out, and_1_out);
endmodule
