// Logisim project fa-1.circ as structural Verilog: 1 circuit, main circuit main
module main (
  input  Input0,
  input  Input1,
  input  CarryIn,
  output Result,
  output CarryOut
);

  wire and_1_out, and_2_out, xor_1_out;

  xor xor_1 (xor_1_out, Input0, Input1);
  and and_1 (and_1_out, Input0, Input1);
  and and_2 (and_2_out, CarryIn, xor_1_out);
  xor xor_2 (Result, xor_1_out, CarryIn);
  or or_1 (CarryOut, and_2_out, and_1_out);
endmodule
