// Logisim project fa-4.circ as structural Verilog: 2 circuits, main circuit main
module main (
  input  Ci,
  input  in_2,
  input  in_3,
  input  in_4,
  input  in_5,
  input  in_6,
  input  in_7,
  input  in_8,
  input  in_9,
  output Sum0,
  output Sum1,
  output Sum2,
  output Sum3,
  output CarryOut
);

  wire fa_1_1_carryout, fa_1_2_carryout, fa_1_3_carryout;

  fa_1 fa_1_1 (.Input0(in_2), .Input1(in_3), .CarryIn(Ci), .Result(Sum0), .CarryOut(fa_1_1_carryout));
  fa_1 fa_1_2 (.Input0(in_4), .Input1(in_5), .CarryIn(fa_1_1_carryout), .Result(Sum1), .CarryOut(fa_1_2_carryout));
  fa_1 fa_1_3 (.Input0(in_6), .Input1(in_7), .CarryIn(fa_1_2_carryout), .Result(Sum2), .CarryOut(fa_1_3_carryout));
  fa_1 fa_1_4 (.Input0(in_8), .Input1(in_9), .CarryIn(fa_1_3_carryout), .Result(Sum3), .CarryOut(CarryOut));
endmodule

module fa_1 (
  input  Input0,
  input  Input1,
  input  CarryIn,
  output Result,
  output CarryOut
);

  wire and_1_out, and_2_out, xor_1_out;

  xor xor_1 (xor_1_out, Input0, Input1);
  and and_1 (and_1_out, Input0, Input1);
  and and_2 (and_2_out, CarryIn, xor_1_out);
  xor xor_2 (Result, xor_1_out, CarryIn);
  or or_1 (CarryOut, and_2_out, and_1_out);
endmodule
