// Logisim project mux-2-8.circ as structural Verilog: 1 circuit, main circuit main
module main (
  input  Selector0,
  input  [7:0] Input0,
  input  [7:0] Input1,
  output [7:0] Output
);

  wire and_1_out, and_2_out, and_3_out, and_4_out, and_5_out, and_6_out, and_7_out, and_8_out, and_9_out,
       and_10_out, and_11_out, and_12_out, and_13_out, and_14_out, and_15_out, and_16_out, not_1_out,
       not_2_out, not_3_out, not_4_out, not_5_out, not_6_out, not_7_out;

  not not_1 (not_1_out, Selector0);
  not not_2 (not_2_out, Selector0);
  not not_3 (not_3_out, Selector0);
  and and_1 (and_1_out, Input0[6], not_1_out);
  buf and_2 (and_2_out, Input0[7]);  // AND_Gate
  and and_3 (and_3_out, Input1[6], Selector0);
  and and_4 (and_4_out, Input1[7], Selector0);
  not not_4 (not_4_out, Selector0);
  and and_5 (and_5_out, Input0[5], not_3_out);
  and and_6 (and_6_out, Input1[5], Selector0);
  not not_5 (not_5_out, Selector0);
  and and_7 (and_7_out, Input0[4], not_2_out);
  and and_8 (and_8_out, Input1[4], Selector0);
  not not_6 (not_6_out, Selector0);
  not not_7 (not_7_out, Selector0);
  and and_9 (and_9_out, Input0[2], not_5_out);
  and and_10 (and_10_out, Input0[3], not_4_out);
  and and_11 (and_11_out, Input1[2], Selector0);
  and and_12 (and_12_out, Input1[3], Selector0);
  and and_13 (and_13_out, Input0[1], not_7_out);
  and and_14 (and_14_out, Input1[1], Selector0);
  and and_15 (and_15_out, Input0[0], not_6_out);
  and and_16 (and_16_out, Input1[0], Selector0);
  or or_1 (Output[3], and_10_out, and_12_out);
  or or_2 (Output[6], and_1_out, and_3_out);
  or or_3 (Output[7], and_2_out, and_4_out);
  or or_4 (Output[2], and_9_out, and_11_out);
  or or_5 (Output[5], and_5_out, and_6_out);
  or or_6 (Output[0], and_15_out, and_16_out);
  or or_7 (Output[1], and_13_out, and_14_out);
  or or_8 (Output[4], and_7_out, and_8_out);
endmodule
