// Logisim project mux-2.circ as structural Verilog: 1 circuit, main circuit main
module main (
  input  Selector,
  input  Input0,
  input  Input1,
  output Output
);

  wire and_1_out, and_2_out, not_1_out;

  not not_1 (not_1_out, Selector);
  and and_1 (and_1_out, Input0, not_1_out);
  and and_2 (and_2_out, Input1, Selector);
  or or_1 (Output, and_1_out, and_2_out);
endmodule
