// Logisim project mux-4i.circ as structural Verilog: 1 circuit, main circuit main
module main (
  input  S0,
  input  S1,
  input  Input0,
  input  Input1,
  input  Input2,
  input  Input3,
  output Output
);

  wire and_1_out, and_2_out, and_3_out, and_4_out, not_1_out, not_2_out, not_3_out, not_4_out;

  not not_1 (not_1_out, S0);
  not not_2 (not_2_out, S0);
  and and_1 (and_1_out, Input0, not_1_out, not_3_out);
  not not_3 (not_3_out, S1);
  and and_2 (and_2_out, Input1, not_2_out, S1);
  and and_3 (and_3_out, Input2, S0, not_4_out);
  not not_4 (not_4_out, S1);
  and and_4 (and_4_out, Input3, S0, S1);
  or or_1 (Output, and_1_out, and_2_out, and_3_out, and_4_out);
endmodule
