// Logisim project mux-4ii.circ as structural Verilog: 2 circuits, main circuit main
module main (
  input  S0,
  input  S1,
  input  Input0,
  input  Input1,
  input  Input2,
  input  Input3,
  output Output
);

  wire mux_2_1_output, mux_2_2_output;

  mux_2 mux_2_1 (.Input0(Input0), .Input1(Input1), .Selector(S1), .Output(mux_2_1_output));
  mux_2 mux_2_2 (.Input0(Input2), .Input1(Input3), .Selector(S1), .Output(mux_2_2_output));
  mux_2 mux_2_3 (.Input0(mux_2_1_output), .Input1(mux_2_2_output), .Selector(S0), .Output(Output));
endmodule

module mux_2 (
  input  Selector,
  input  Input0,
  input  Input1,
  output Output
);

  wire and_1_out, and_2_out, not_1_out;

  not not_1 (not_1_out, Selector);
  and and_1 (and_1_out, Input0, not_1_out);
  and and_2 (and_2_out, Input1, Selector);
  or or_1 (Output, and_1_out, and_2_out);
endmodule
