// Logisim project lab3.circ as structural Verilog: 11 circuits, main circuit CLA1-
module CLA1 (
  input  Cin,
  input  A,
  input  B,
  output S,
  output P,
  output G
);

  wire and_2_out, and_3_out, and_4_out, not_1_out, not_2_out, not_3_out;

  not not_1 (not_1_out, B);
  not not_2 (not_2_out, A);
  not not_3 (not_3_out, Cin);
  and and_1 (G, A, B);
  and and_2 (and_2_out, A, not_1_out);
  and and_3 (and_3_out, Cin, not_2_out);
  and and_4 (and_4_out, B, not_3_out);
  or or_1 (S, and_2_out, and_3_out, and_4_out);
  or or_2 (P, A, B);
endmodule

module CLA1_2 (
  input  Cin,
  input  A,
  input  B,
  output S,
  output P,
  output G,
  output Co
);

  wire and_2_out, and_3_out, and_4_out, and_5_out, not_1_out, not_2_out, not_3_out;

  not not_1 (not_1_out, B);
  not not_2 (not_2_out, A);
  not not_3 (not_3_out, Cin);
  and and_1 (G, A, B);
  and and_2 (and_2_out, A, not_1_out);
  and and_3 (and_3_out, Cin, not_2_out);
  and and_4 (and_4_out, B, not_3_out);
  or or_1 (S, and_2_out, and_3_out, and_4_out);
  or or_2 (P, A, B);
  and and_5 (and_5_out, P, Cin);
  or or_3 (Co, G, and_5_out);
endmodule

module CL_Block (
  input  C0_Cin,
  input  Pin0,
  input  Gin0,
  input  Pin1,
  input  Gin1,
  input  Pin2,
  input  Gin2,
  output C1,
  output C2,
  output C3_Cout,
  output Pout,
  output Gout
);

  wire and_1_out, and_2_out, and_3_out, and_4_out, and_5_out, and_6_out, and_8_out, and_9_out;

  and and_1 (and_1_out, Pin0, C0_Cin);
  and and_2 (and_2_out, Pin1, Gin0);
  and and_3 (and_3_out, Pin1, Pin0, C0_Cin);
  and and_4 (and_4_out, Pin2, Gin1);
  and and_5 (and_5_out, Pin2, Pin1, Gin0);
  and and_6 (and_6_out, Pin2, Pin1, Pin0, C0_Cin);
  and and_7 (Pout, Pin2, Pin1, Pin0);
  and and_8 (and_8_out, Pin2, Gin1);
  and and_9 (and_9_out, Pin2, Pin1, Gin0);
  or or_1 (C1, and_1_out, Gin0);
  or or_2 (C2, and_2_out, and_3_out, Gin1);
  or or_3 (C3_Cout, and_4_out, Gin2, and_5_out, and_6_out);
  or or_4 (Gout, and_8_out, Gin2, and_9_out);
endmodule

module CL_Block_2 (
  input  C0_Cin,
  input  Pin0,
  input  Gin0,
  input  Pin1,
  input  Gin1,
  input  Pin2,
  input  Gin2,
  output C1,
  output C2,
  output Pout,
  output Gout
);

  wire and_1_out, and_2_out, and_3_out, and_5_out, and_6_out;

  and and_1 (and_1_out, Pin0, C0_Cin);
  and and_2 (and_2_out, Pin1, Gin0);
  and and_3 (and_3_out, Pin1, Pin0, C0_Cin);
  and and_4 (Pout, Pin2, Pin1, Pin0);
  and and_5 (and_5_out, Pin2, Gin1);
  and and_6 (and_6_out, Pin2, Pin1, Gin0);
  or or_1 (C1, and_1_out, Gin0);
  or or_2 (C2, and_2_out, and_3_out, Gin1);
  or or_3 (Gout, and_5_out, Gin2, and_6_out);
endmodule

module CLA3 (
  input  Cin,
  input  A0,
  input  B0,
  input  A1,
  input  B1,
  input  A2,
  input  B2,
  output S0,
  output P,
  output G,
  output S1,
  output S2
);

  wire cl_block_1_c1, cl_block_1_c2, cla1_1_g, cla1_1_p, cla1_2_g, cla1_2_p, cla1_3_g, cla1_3_p;

  CLA1 cla1_1 (.A(A0), .B(B0), .Cin(Cin), .S(S0), .P(cla1_1_p), .G(cla1_1_g));
  CLA1 cla1_2 (.A(A1), .B(B1), .Cin(cl_block_1_c1), .S(S1), .P(cla1_2_p), .G(cla1_2_g));
  CLA1 cla1_3 (.A(A2), .B(B2), .Cin(cl_block_1_c2), .S(S2), .P(cla1_3_p), .G(cla1_3_g));
  CL_Block_2 cl_block_1 (
    .Pin0(cla1_1_p), .Gin0(cla1_1_g), .C1(cl_block_1_c1), .Pin1(cla1_2_p), .Gin1(cla1_2_g),
    .C2(cl_block_1_c2), .Pin2(cla1_3_p), .Gin2(cla1_3_g), .C0_Cin(Cin), .Pout(P), .Gout(G));
endmodule

module CLA3_2 (
  input  Cin,
  input  A0,
  input  B0,
  input  A1,
  input  B1,
  input  A2,
  input  B2,
  output S0,
  output P,
  output G,
  output S1,
  output S2,
  output Cout
);

  wire cl_block_1_c1, cl_block_1_c2, cla1_1_g, cla1_1_p, cla1_2_g, cla1_2_p, cla1_3_g, cla1_3_p;

  CLA1_2 cla1_1 (.A(A0), .B(B0), .Cin(Cin), .S(S0), .P(cla1_1_p), .G(cla1_1_g));  // open: Co
  CLA1_2 cla1_2 (.A(A1), .B(B1), .Cin(cl_block_1_c1), .S(S1), .P(cla1_2_p), .G(cla1_2_g));  // open: Co
  CLA1_2 cla1_3 (.A(A2), .B(B2), .Cin(cl_block_1_c2), .S(S2), .P(cla1_3_p), .G(cla1_3_g));  // open: Co
  CL_Block cl_block_1 (
    .Pin0(cla1_1_p), .Gin0(cla1_1_g), .C1(cl_block_1_c1), .Pin1(cla1_2_p), .Gin1(cla1_2_g),
    .C2(cl_block_1_c2), .Pin2(cla1_3_p), .Gin2(cla1_3_g), .C3_Cout(Cout), .C0_Cin(Cin), .Pout(P), .Gout(G));
endmodule

module CLA9 (
  input  Cin,
  input  A0,
  input  B0,
  input  A1,
  input  B1,
  input  A2,
  input  B2,
  input  A3,
  input  B3,
  input  A4,
  input  B4,
  input  A5,
  input  B5,
  input  A6,
  input  B6,
  input  A7,
  input  B7,
  input  A8,
  input  B8,
  output S0,
  output S1,
  output S2,
  output S3,
  output S4,
  output S5,
  output P,
  output G,
  output S6,
  output S7,
  output S8
);

  wire cl_block_1_c1, cl_block_1_c2, cla3_1_g, cla3_1_p, cla3_2_g, cla3_2_p, cla3_3_g, cla3_3_p;

  CLA3 cla3_1 (
    .A0(A0), .B0(B0), .A1(A1), .B1(B1), .A2(A2), .B2(B2), .Cin(Cin), .S0(S0), .P(cla3_1_p), .G(cla3_1_g),
    .S1(S1), .S2(S2));
  CLA3 cla3_2 (
    .A0(A3), .B0(B3), .A1(A4), .B1(B4), .A2(A5), .B2(B5), .Cin(cl_block_1_c1), .S0(S3), .P(cla3_2_p),
    .G(cla3_2_g), .S1(S4), .S2(S5));
  CLA3 cla3_3 (
    .A0(A6), .B0(B6), .A1(A7), .B1(B7), .A2(A8), .B2(B8), .Cin(cl_block_1_c2), .S0(S6), .P(cla3_3_p),
    .G(cla3_3_g), .S1(S7), .S2(S8));
  CL_Block_2 cl_block_1 (
    .Pin0(cla3_1_p), .Gin0(cla3_1_g), .C1(cl_block_1_c1), .Pin1(cla3_2_p), .Gin1(cla3_2_g),
    .C2(cl_block_1_c2), .Pin2(cla3_3_p), .Gin2(cla3_3_g), .C0_Cin(Cin), .Pout(P), .Gout(G));
endmodule

module CLA9_2 (
  input  Cin,
  input  A0,
  input  B0,
  input  A1,
  input  B1,
  input  A2,
  input  B2,
  input  A3,
  input  B3,
  input  A4,
  input  B4,
  input  A5,
  input  B5,
  input  A6,
  input  B6,
  input  A7,
  input  B7,
  input  A8,
  input  B8,
  output S0,
  output S1,
  output S2,
  output S3,
  output S4,
  output S5,
  output P,
  output G,
  output S6,
  output S7,
  output S8,
  output Cout
);

  wire cl_block_1_c1, cl_block_1_c2, cla3_1_g, cla3_1_p, cla3_2_g, cla3_2_p, cla3_3_g, cla3_3_p;

  CLA3_2 cla3_1 (
    .A0(A0), .B0(B0), .A1(A1), .B1(B1), .A2(A2), .B2(B2), .Cin(Cin), .S0(S0), .P(cla3_1_p), .G(cla3_1_g),
    .S1(S1), .S2(S2));  // open: Cout
  CLA3_2 cla3_2 (
    .A0(A3), .B0(B3), .A1(A4), .B1(B4), .A2(A5), .B2(B5), .Cin(cl_block_1_c1), .S0(S3), .P(cla3_2_p),
    .G(cla3_2_g), .S1(S4), .S2(S5));  // open: Cout
  CLA3_2 cla3_3 (
    .A0(A6), .B0(B6), .A1(A7), .B1(B7), .A2(A8), .B2(B8), .Cin(cl_block_1_c2), .S0(S6), .P(cla3_3_p),
    .G(cla3_3_g), .S1(S7), .S2(S8));  // open: Cout
  CL_Block cl_block_1 (
    .Pin0(cla3_1_p), .Gin0(cla3_1_g), .C1(cl_block_1_c1), .Pin1(cla3_2_p), .Gin1(cla3_2_g),
    .C2(cl_block_1_c2), .Pin2(cla3_3_p), .Gin2(cla3_3_g), .C3_Cout(Cout), .C0_Cin(Cin), .Pout(P), .Gout(G));
endmodule

module CLA27 (
  input  Cin,
  input  A0,
  input  B0,
  input  A1,
  input  B1,
  input  A2,
  input  B2,
  input  A3,
  input  B3,
  input  A4,
  input  B4,
  input  A5,
  input  B5,
  input  A6,
  input  B6,
  input  A7,
  input  B7,
  input  A8,
  input  B8,
  input  A9,
  input  B9,
  input  A10,
  input  B10,
  input  A11,
  input  B11,
  input  A12,
  input  B12,
  input  A13,
  input  B13,
  input  A14,
  input  B14,
  input  A15,
  input  B15,
  input  A16,
  input  B16,
  input  A17,
  input  B17,
  input  A18,
  input  B18,
  input  A19,
  input  B19,
  input  A20,
  input  B20,
  input  A21,
  input  B21,
  input  A22,
  input  B22,
  input  A23,
  input  B23,
  input  A24,
  input  B24,
  input  A25,
  input  B25,
  input  A26,
  input  B26,
  output S0,
  output S1,
  output S2,
  output S3,
  output S4,
  output S5,
  output S6,
  output S7,
  output S8,
  output S9,
  output S10,
  output S11,
  output S12,
  output S13,
  output P,
  output G,
  output S14,
  output S15,
  output S16,
  output S17,
  output S18,
  output S19,
  output S20,
  output S21,
  output S22,
  output S23,
  output S24,
  output S25,
  output S26
);

  wire cl_block_1_c1, cl_block_1_c2, cla9_1_g, cla9_1_p, cla9_2_g, cla9_2_p, cla9_3_g, cla9_3_p;

  CLA9 cla9_1 (
    .A0(A0), .B0(B0), .A1(A1), .B1(B1), .A2(A2), .B2(B2), .A3(A3), .B3(B3), .A4(A4), .B4(B4), .A5(A5),
    .B5(B5), .A6(A6), .B6(B6), .A7(A7), .B7(B7), .A8(A8), .B8(B8), .Cin(Cin), .S0(S0), .S1(S1), .S2(S2),
    .S3(S3), .S4(S4), .S5(S5), .P(cla9_1_p), .G(cla9_1_g), .S6(S6), .S7(S7), .S8(S8));
  CLA9 cla9_2 (
    .A0(A9), .B0(B9), .A1(A10), .B1(B10), .A2(A11), .B2(B11), .A3(A12), .B3(B12), .A4(A13), .B4(B13),
    .A5(A14), .B5(B14), .A6(A15), .B6(B15), .A7(A16), .B7(B16), .A8(A17), .B8(B17), .Cin(cl_block_1_c1),
    .S0(S9), .S1(S10), .S2(S11), .S3(S12), .S4(S13), .S5(S14), .P(cla9_2_p), .G(cla9_2_g), .S6(S15),
    .S7(S16), .S8(S17));
  CLA9 cla9_3 (
    .A0(A18), .B0(B18), .A1(A19), .B1(B19), .A2(A20), .B2(B20), .A3(A21), .B3(B21), .A4(A22), .B4(B22),
    .A5(A23), .B5(B23), .A6(A24), .B6(B24), .A7(A25), .B7(B25), .A8(A26), .B8(B26), .Cin(cl_block_1_c2),
    .S0(S18), .S1(S19), .S2(S20), .S3(S21), .S4(S22), .S5(S23), .P(cla9_3_p), .G(cla9_3_g), .S6(S24),
    .S7(S25), .S8(S26));
  CL_Block_2 cl_block_1 (
    .Pin0(cla9_1_p), .Gin0(cla9_1_g), .C1(cl_block_1_c1), .Pin1(cla9_2_p), .Gin1(cla9_2_g),
    .C2(cl_block_1_c2), .Pin2(cla9_3_p), .Gin2(cla9_3_g), .C0_Cin(Cin), .Pout(P), .Gout(G));
endmodule

module CLA27_2 (
  input  Cin,
  input  A0,
  input  B0,
  input  A1,
  input  B1,
  input  A2,
  input  B2,
  input  A3,
  input  B3,
  input  A4,
  input  B4,
  input  A5,
  input  B5,
  input  A6,
  input  B6,
  input  A7,
  input  B7,
  input  A8,
  input  B8,
  input  A9,
  input  B9,
  input  A10,
  input  B10,
  input  A11,
  input  B11,
  input  A12,
  input  B12,
  input  A13,
  input  B13,
  input  A14,
  input  B14,
  input  A15,
  input  B15,
  input  A16,
  input  B16,
  input  A17,
  input  B17,
  input  A18,
  input  B18,
  input  A19,
  input  B19,
  input  A20,
  input  B20,
  input  A21,
  input  B21,
  input  A22,
  input  B22,
  input  A23,
  input  B23,
  input  A24,
  input  B24,
  input  A25,
  input  B25,
  input  A26,
  input  B26,
  output S0,
  output S1,
  output S2,
  output S3,
  output S4,
  output S5,
  output S6,
  output S7,
  output S8,
  output S9,
  output S10,
  output S11,
  output S12,
  output S13,
  output P,
  output G,
  output S14,
  output S15,
  output S16,
  output S17,
  output S18,
  output S19,
  output S20,
  output S21,
  output S22,
  output S23,
  output S24,
  output S25,
  output S26,
  output Cout
);

  wire cl_block_1_c1, cl_block_1_c2, cla9_1_g, cla9_1_p, cla9_2_g, cla9_2_p, cla9_3_g, cla9_3_p;

  CLA9_2 cla9_1 (
    .A0(A0), .B0(B0), .A1(A1), .B1(B1), .A2(A2), .B2(B2), .A3(A3), .B3(B3), .A4(A4), .B4(B4), .A5(A5),
    .B5(B5), .A6(A6), .B6(B6), .A7(A7), .B7(B7), .A8(A8), .B8(B8), .Cin(Cin), .S0(S0), .S1(S1), .S2(S2),
    .S3(S3), .S4(S4), .S5(S5), .P(cla9_1_p), .G(cla9_1_g), .S6(S6), .S7(S7), .S8(S8));  // open: Cout
  CLA9_2 cla9_2 (
    .A0(A9), .B0(B9), .A1(A10), .B1(B10), .A2(A11), .B2(B11), .A3(A12), .B3(B12), .A4(A13), .B4(B13),
    .A5(A14), .B5(B14), .A6(A15), .B6(B15), .A7(A16), .B7(B16), .A8(A17), .B8(B17), .Cin(cl_block_1_c1),
    .S0(S9), .S1(S10), .S2(S11), .S3(S12), .S4(S13), .S5(S14), .P(cla9_2_p), .G(cla9_2_g), .S6(S15),
    .S7(S16), .S8(S17));  // open: Cout
  CLA9_2 cla9_3 (
    .A0(A18), .B0(B18), .A1(A19), .B1(B19), .A2(A20), .B2(B20), .A3(A21), .B3(B21), .A4(A22), .B4(B22),
    .A5(A23), .B5(B23), .A6(A24), .B6(B24), .A7(A25), .B7(B25), .A8(A26), .B8(B26), .Cin(cl_block_1_c2),
    .S0(S18), .S1(S19), .S2(S20), .S3(S21), .S4(S22), .S5(S23), .P(cla9_3_p), .G(cla9_3_g), .S6(S24),
    .S7(S25), .S8(S26));  // open: Cout
  CL_Block cl_block_1 (
    .Pin0(cla9_1_p), .Gin0(cla9_1_g), .C1(cl_block_1_c1), .Pin1(cla9_2_p), .Gin1(cla9_2_g),
    .C2(cl_block_1_c2), .Pin2(cla9_3_p), .Gin2(cla9_3_g), .C3_Cout(Cout), .C0_Cin(Cin), .Pout(P), .Gout(G));
endmodule

module CLA27_2_2 (
  input  Cin,
  input  A0,
  input  B0,
  input  A1,
  input  B1,
  input  A2,
  input  B2,
  input  A3,
  input  B3,
  input  A4,
  input  B4,
  input  A5,
  input  B5,
  input  A6,
  input  B6,
  input  A7,
  input  B7,
  input  A8,
  input  B8,
  input  A9,
  input  B9,
  input  A10,
  input  B10,
  input  A11,
  input  B11,
  input  A12,
  input  B12,
  input  A13,
  input  B13,
  input  A14,
  input  B14,
  input  A15,
  input  B15,
  input  A16,
  input  B16,
  input  A17,
  input  B17,
  input  A18,
  input  B18,
  input  A19,
  input  B19,
  input  A20,
  input  B20,
  input  A21,
  input  B21,
  input  A22,
  input  B22,
  input  A23,
  input  B23,
  input  A24,
  input  B24,
  input  A25,
  input  B25,
  input  A26,
  input  B26,
  output S0,
  output S1,
  output S2,
  output S3,
  output S4,
  output S5,
  output S6,
  output S7,
  output S8,
  output S9,
  output S10,
  output S11,
  output S12,
  output S13,
  output P,
  output G,
  output S14,
  output S15,
  output S16,
  output S17,
  output S18,
  output S19,
  output S20,
  output S21,
  output S22,
  output S23,
  output S24,
  output S25,
  output S26,
  output Cout
);

  wire cl_block_1_c1, cl_block_1_c2, cla9_1_g, cla9_1_p, cla9_2_g, cla9_2_p, cla9_3_g, cla9_3_p;

  CLA9 cla9_1 (
    .A0(A0), .B0(B0), .A1(A1), .B1(B1), .A2(A2), .B2(B2), .A3(A3), .B3(B3), .A4(A4), .B4(B4), .A5(A5),
    .B5(B5), .A6(A6), .B6(B6), .A7(A7), .B7(B7), .A8(A8), .B8(B8), .Cin(Cin), .S0(S0), .S1(S1), .S2(S2),
    .S3(S3), .S4(S4), .S5(S5), .P(cla9_1_p), .G(cla9_1_g), .S6(S6), .S7(S7), .S8(S8));
  CLA9 cla9_2 (
    .A0(A9), .B0(B9), .A1(A10), .B1(B10), .A2(A11), .B2(B11), .A3(A12), .B3(B12), .A4(A13), .B4(B13),
    .A5(A14), .B5(B14), .A6(A15), .B6(B15), .A7(A16), .B7(B16), .A8(A17), .B8(B17), .Cin(cl_block_1_c1),
    .S0(S9), .S1(S10), .S2(S11), .S3(S12), .S4(S13), .S5(S14), .P(cla9_2_p), .G(cla9_2_g), .S6(S15),
    .S7(S16), .S8(S17));
  CLA9 cla9_3 (
    .A0(A18), .B0(B18), .A1(A19), .B1(B19), .A2(A20), .B2(B20), .A3(A21), .B3(B21), .A4(A22), .B4(B22),
    .A5(A23), .B5(B23), .A6(A24), .B6(B24), .A7(A25), .B7(B25), .A8(A26), .B8(B26), .Cin(cl_block_1_c2),
    .S0(S18), .S1(S19), .S2(S20), .S3(S21), .S4(S22), .S5(S23), .P(cla9_3_p), .G(cla9_3_g), .S6(S24),
    .S7(S25), .S8(S26));
  CL_Block cl_block_1 (
    .Pin0(cla9_1_p), .Gin0(cla9_1_g), .C1(cl_block_1_c1), .Pin1(cla9_2_p), .Gin1(cla9_2_g),
    .C2(cl_block_1_c2), .Pin2(cla9_3_p), .Gin2(cla9_3_g), .C3_Cout(Cout), .C0_Cin(Cin), .Pout(P), .Gout(G));
endmodule
