// Logisim project 2Flop-2Wide-2Read-1Write.circ as structural Verilog: 1 circuit, main circuit main
module main (
  input  ReadReg1,
  input  Clock,
  input  WriteReg,
  input  [1:0] WriteData,
  input  ReadReg2,
  input  RegWrite,
  output [1:0] RegData1,
  output [1:0] RegData2
);

  wire d_ff_1_q, d_ff_2_q, d_ff_3_q, d_ff_4_q, decoder_1_out0, decoder_1_out1, not_1_out, not_2_out,
       or_1_out, or_2_out;

  Decoder #(.enable("false")) decoder_1 (.out0(decoder_1_out0), .out1(decoder_1_out1), .sel(WriteReg));
  not not_1 (not_1_out, RegWrite);
  not not_2 (not_2_out, RegWrite);
  or or_1 (or_1_out, not_1_out, Clock);
  or or_2 (or_2_out, not_2_out, Clock);
  D_Flip_Flop #(.trigger("falling")) d_ff_1 (
    .clk(or_1_out), .D(WriteData[0]), .Q(d_ff_1_q), .en(decoder_1_out0));  // open: Qn, preset, reset
  D_Flip_Flop #(.trigger("falling")) d_ff_2 (
    .clk(or_1_out), .D(WriteData[1]), .Q(d_ff_2_q), .en(decoder_1_out0));  // open: Qn, preset, reset
  D_Flip_Flop #(.trigger("falling")) d_ff_3 (
    .clk(or_2_out), .D(WriteData[0]), .Q(d_ff_3_q), .en(decoder_1_out1));  // open: Qn, preset, reset
  D_Flip_Flop #(.trigger("falling")) d_ff_4 (
    .clk(or_2_out), .D(WriteData[1]), .Q(d_ff_4_q), .en(decoder_1_out1));  // open: Qn, preset, reset
  Multiplexer #(.enable("false")) multiplexer_1 (.in0(d_ff_1_q), .in1(d_ff_3_q), .out(RegData1[0]), .sel(ReadReg1));
  Multiplexer #(.enable("false")) multiplexer_2 (.in0(d_ff_2_q), .in1(d_ff_4_q), .out(RegData1[1]), .sel(ReadReg1));
  Multiplexer #(.enable("false")) multiplexer_3 (.in0(d_ff_1_q), .in1(d_ff_3_q), .out(RegData2[0]), .sel(ReadReg2));
  Multiplexer #(.enable("false")) multiplexer_4 (.in0(d_ff_2_q), .in1(d_ff_4_q), .out(RegData2[1]), .sel(ReadReg2));
endmodule
