// Logisim project 2Flop-2Wide-2Read.circ as structural Verilog: 1 circuit, main circuit reg-file
module reg_file (
  input  ReadReg1,
  input  ReadReg2,
  input  Clock,
  output [1:0] RegData1,
  output [1:0] RegData2
);

  wire d_ff_1_q, d_ff_2_q, d_ff_3_q, d_ff_4_q;

  D_Flip_Flop #(.trigger("falling")) d_ff_1 (.Q(d_ff_1_q));  // open: clk, D, Qn, preset, en, reset
  D_Flip_Flop #(.trigger("falling")) d_ff_2 (.Q(d_ff_2_q));  // open: clk, D, Qn, preset, en, reset
  D_Flip_Flop #(.trigger("falling")) d_ff_3 (.Q(d_ff_3_q));  // open: clk, D, Qn, preset, en, reset
  D_Flip_Flop #(.trigger("falling")) d_ff_4 (.Q(d_ff_4_q));  // open: clk, D, Qn, preset, en, reset
  Multiplexer #(.enable("false")) multiplexer_1 (.in0(d_ff_1_q), .in1(d_ff_3_q), .out(RegData1[0]), .sel(ReadReg1));
  Multiplexer #(.enable("false")) multiplexer_2 (.in0(d_ff_2_q), .in1(d_ff_4_q), .out(RegData1[1]), .sel(ReadReg1));
  Multiplexer #(.enable("false")) multiplexer_3 (.in0(d_ff_1_q), .in1(d_ff_3_q), .out(RegData2[0]), .sel(ReadReg2));
  Multiplexer #(.enable("false")) multiplexer_4 (.in0(d_ff_2_q), .in1(d_ff_4_q), .out(RegData2[1]), .sel(ReadReg2));
endmodule
