// Logisim project alu-4bit.circ as structural Verilog: 5 circuits, main circuit fa-1
module fa_1 (
  input  Input0,
  input  Input1,
  input  CarryIn,
  output Result,
  output CarryOut
);

  wire and_1_out, and_2_out, xor_1_out;

  xor xor_1 (xor_1_out, Input0, Input1);
  and and_1 (and_1_out, Input0, Input1);
  and and_2 (and_2_out, CarryIn, xor_1_out);
  xor xor_2 (Result, xor_1_out, CarryIn);
  or or_1 (CarryOut, and_2_out, and_1_out);
endmodule

module alu_1 (
  input  [1:0] Operation,
  input  Ainvert,
  input  Binvert,
  input  Cin,
  input  A,
  input  B,
  input  Less,
  output Result,
  output Set,
  output Overflow,
  output Cout
);

  wire and_1_out, fa_1_1_result, mux_2_1_output, mux_2_2_output, not_1_out, not_2_out, or_1_out;

  mux_2 mux_2_1 (.Input0(A), .Input1(not_1_out), .Selector(Ainvert), .Output(mux_2_1_output));
  not not_1 (not_1_out, A);
  not not_2 (not_2_out, B);
  mux_2 mux_2_2 (.Input0(B), .Input1(not_2_out), .Selector(Binvert), .Output(mux_2_2_output));
  and and_1 (and_1_out, mux_2_1_output, mux_2_2_output);
  or or_1 (or_1_out, mux_2_1_output, mux_2_2_output);
  fa_1 fa_1_1 (
    .Input0(mux_2_1_output), .Input1(mux_2_2_output), .CarryIn(Cin), .Result(fa_1_1_result), .CarryOut(Cout));
  mux_4i mux_4i_1 (
    .Input0(and_1_out), .Input1(or_1_out), .Input2(fa_1_1_result), .Input3(Less), .S0(Operation[1]),
    .S1(Operation[0]), .Output(Result));
  xor xor_1 (Overflow, Cin, Cout);
  xor xor_2 (Set, fa_1_1_result, Overflow);
endmodule

module mux_4i (
  input  S0,
  input  S1,
  input  Input0,
  input  Input1,
  input  Input2,
  input  Input3,
  output Output
);

  wire and_1_out, and_2_out, and_3_out, and_4_out, not_1_out, not_2_out, not_3_out, not_4_out;

  not not_1 (not_1_out, S0);
  not not_2 (not_2_out, S0);
  and and_1 (and_1_out, Input0, not_1_out, not_3_out);
  not not_3 (not_3_out, S1);
  and and_2 (and_2_out, Input1, not_2_out, S1);
  and and_3 (and_3_out, Input2, S0, not_4_out);
  not not_4 (not_4_out, S1);
  and and_4 (and_4_out, Input3, S0, S1);
  or or_1 (Output, and_1_out, and_2_out, and_3_out, and_4_out);
endmodule

module mux_2 (
  input  Selector,
  input  Input0,
  input  Input1,
  output Output
);

  wire and_1_out, and_2_out, not_1_out;

  not not_1 (not_1_out, Selector);
  and and_1 (and_1_out, Input0, not_1_out);
  and and_2 (and_2_out, Input1, Selector);
  or or_1 (Output, and_1_out, and_2_out);
endmodule

module alu_4 (
  input  Ainvert,
  input  Bnegate,
  input  [1:0] Operation,
  input  [3:0] A,
  input  [3:0] B,
  input  Less,
  output [3:0] Result,
  output Equal_Zero,
  output Overflow,
  output CarryOut
);

  wire alu_1_1_cout, alu_1_2_cout, alu_1_3_cout, alu_1_4_set;

  alu_1 alu_1_1 (
    .A(A[0]), .B(B[0]), .Less(alu_1_4_set), .Ainvert(Ainvert), .Binvert(Bnegate), .Cin(Bnegate),
    .Operation(Operation), .Cout(alu_1_1_cout), .Result(Result[0]));  // open: Set, Overflow
  alu_1 alu_1_2 (
    .A(A[1]), .B(B[1]), .Less(Less), .Ainvert(Ainvert), .Binvert(Bnegate), .Cin(alu_1_1_cout),
    .Operation(Operation), .Cout(alu_1_2_cout), .Result(Result[1]));  // open: Set, Overflow
  alu_1 alu_1_3 (
    .A(A[2]), .B(B[2]), .Less(Less), .Ainvert(Ainvert), .Binvert(Bnegate), .Cin(alu_1_2_cout),
    .Operation(Operation), .Cout(alu_1_3_cout), .Result(Result[2]));  // open: Set, Overflow
  alu_1 alu_1_4 (
    .A(A[3]), .B(B[3]), .Less(Less), .Ainvert(Ainvert), .Binvert(Bnegate), .Cin(alu_1_3_cout),
    .Operation(Operation), .Cout(CarryOut), .Result(Result[3]), .Set(alu_1_4_set), .Overflow(Overflow));
  nor nor_1 (Equal_Zero, Result[0], Result[1], Result[2], Overflow);
endmodule
