// Logisim project Adder-32.circ as structural Verilog: 6 circuits, main circuit mux-2
module mux_2 (
  input  Selector,
  input  Input0,
  input  Input1,
  output Output
);

  wire and_1_out, and_2_out, not_1_out;

  not not_1 (not_1_out, Selector);
  and and_1 (and_1_out, Input0, not_1_out);
  and and_2 (and_2_out, Input1, Selector);
  or or_1 (Output, and_1_out, and_2_out);
endmodule

module mux_4i (
  input  S0,
  input  S1,
  input  Input0,
  input  Input1,
  input  Input2,
  input  Input3,
  output Output
);

  wire and_1_out, and_2_out, and_3_out, and_4_out, not_1_out, not_2_out, not_3_out, not_4_out;

  not not_1 (not_1_out, S0);
  not not_2 (not_2_out, S0);
  and and_1 (and_1_out, Input0, not_1_out, not_3_out);
  not not_3 (not_3_out, S1);
  and and_2 (and_2_out, Input1, not_2_out, S1);
  and and_3 (and_3_out, Input2, S0, not_4_out);
  not not_4 (not_4_out, S1);
  and and_4 (and_4_out, Input3, S0, S1);
  or or_1 (Output, and_1_out, and_2_out, and_3_out, and_4_out);
endmodule

module fa_1 (
  input  Input0,
  input  Input1,
  input  CarryIn,
  output Result,
  output CarryOut
);

  wire and_1_out, and_2_out, xor_1_out;

  xor xor_1 (xor_1_out, Input0, Input1);
  and and_1 (and_1_out, Input0, Input1);
  and and_2 (and_2_out, CarryIn, xor_1_out);
  xor xor_2 (Result, xor_1_out, CarryIn);
  or or_1 (CarryOut, and_2_out, and_1_out);
endmodule

module alu_1 (
  input  [1:0] Operation,
  input  Binvert,
  input  Cin,
  input  A,
  input  B,
  input  Less,
  output Result,
  output Set,
  output Overflow,
  output Cout
);

  wire and_1_out, fa_1_1_result, mux_2_1_output, not_1_out, or_1_out;

  not not_1 (not_1_out, B);
  mux_2 mux_2_1 (.Input0(B), .Input1(not_1_out), .Selector(Binvert), .Output(mux_2_1_output));
  and and_1 (and_1_out, A, mux_2_1_output);
  or or_1 (or_1_out, A, mux_2_1_output);
  fa_1 fa_1_1 (.Input0(A), .Input1(mux_2_1_output), .CarryIn(Cin), .Result(fa_1_1_result), .CarryOut(Cout));
  mux_4i mux_4i_1 (
    .Input0(and_1_out), .Input1(or_1_out), .Input2(fa_1_1_result), .Input3(Less), .S0(Operation[1]),
    .S1(Operation[0]), .Output(Result));
  xor xor_1 (Overflow, Cin, Cout);
  xor xor_2 (Set, fa_1_1_result, Overflow);
endmodule

module alu_8 (
  input  Bnegate,
  input  Cin,
  input  [1:0] Operation,
  input  A0,
  input  B0,
  input  A1,
  input  B1,
  input  A2,
  input  B2,
  input  A3,
  input  B3,
  input  A4,
  input  B4,
  input  A5,
  input  B5,
  input  A6,
  input  B6,
  input  A7,
  input  B7,
  input  Less,
  output Result0,
  output Result1,
  output Result2,
  output Result3,
  output Result4,
  output Result5,
  output Result6,
  output Result7,
  output Set,
  output Overflow,
  output Cout
);

  wire alu_1_1_cout, alu_1_2_cout, alu_1_3_cout, alu_1_4_cout, alu_1_5_cout, alu_1_6_cout, alu_1_7_cout,
       not_1_out;

  not not_1 (not_1_out, 1'b1);
  alu_1 alu_1_1 (
    .A(A0), .B(B0), .Less(Less), .Binvert(Bnegate), .Cin(Cin), .Operation(Operation), .Cout(alu_1_1_cout),
    .Result(Result0));  // open: Set, Overflow
  alu_1 alu_1_2 (
    .A(A1), .B(B1), .Less(not_1_out), .Binvert(Bnegate), .Cin(alu_1_1_cout), .Operation(Operation),
    .Cout(alu_1_2_cout), .Result(Result1));  // open: Set, Overflow
  alu_1 alu_1_3 (
    .A(A2), .B(B2), .Less(not_1_out), .Binvert(Bnegate), .Cin(alu_1_2_cout), .Operation(Operation),
    .Cout(alu_1_3_cout), .Result(Result2));  // open: Set, Overflow
  alu_1 alu_1_4 (
    .A(A3), .B(B3), .Less(not_1_out), .Binvert(Bnegate), .Cin(alu_1_3_cout), .Operation(Operation),
    .Cout(alu_1_4_cout), .Result(Result3));  // open: Set, Overflow
  alu_1 alu_1_5 (
    .A(A4), .B(B4), .Less(not_1_out), .Binvert(Bnegate), .Cin(alu_1_4_cout), .Operation(Operation),
    .Cout(alu_1_5_cout), .Result(Result4));  // open: Set, Overflow
  alu_1 alu_1_6 (
    .A(A5), .B(B5), .Less(not_1_out), .Binvert(Bnegate), .Cin(alu_1_5_cout), .Operation(Operation),
    .Cout(alu_1_6_cout), .Result(Result5));  // open: Set, Overflow
  alu_1 alu_1_7 (
    .A(A6), .B(B6), .Less(not_1_out), .Binvert(Bnegate), .Cin(alu_1_6_cout), .Operation(Operation),
    .Cout(alu_1_7_cout), .Result(Result6));  // open: Set, Overflow
  alu_1 alu_1_8 (
    .A(A7), .B(B7), .Less(not_1_out), .Binvert(Bnegate), .Cin(alu_1_7_cout), .Operation(Operation),
    .Cout(Cout), .Result(Result7), .Set(Set), .Overflow(Overflow));
endmodule

module alu_32 (
  input  [31:0] A,
  input  [31:0] B,
  output [31:0] Result,
  output Equal_Zero,
  output Overflow,
  output CarryOut
);

  wire alu_8_1_cout, alu_8_2_cout, alu_8_3_cout, alu_8_4_set, not_1_out, not_2_out;
  wire [0:0] not_3_out;

  not not_1 (not_1_out, 1'b1);
  not not_2 (not_2_out, 1'b1);
  not not_3 (not_3_out[0], 1'b1);
  alu_8 alu_8_1 (
    .A0(A[0]), .B0(B[0]), .A1(A[1]), .B1(B[1]), .A2(A[2]), .B2(B[2]), .A3(A[3]), .B3(B[3]), .A4(A[4]),
    .B4(B[4]), .A5(A[5]), .B5(B[5]), .A6(A[6]), .B6(B[6]), .A7(A[7]), .B7(B[7]), .Less(alu_8_4_set),
    .Bnegate(not_2_out), .Cin(not_2_out), .Operation({1'b1, not_3_out[0]}), .Cout(alu_8_1_cout),
    .Result0(Result[0]), .Result1(Result[1]), .Result2(Result[2]), .Result3(Result[3]), .Result4(Result[4]),
    .Result5(Result[5]), .Result6(Result[6]), .Result7(Result[7]));  // open: Set, Overflow
  alu_8 alu_8_2 (
    .A0(A[8]), .B0(B[8]), .A1(A[9]), .B1(B[9]), .A2(A[10]), .B2(B[10]), .A3(A[11]), .B3(B[11]), .A4(A[12]),
    .B4(B[12]), .A5(A[13]), .B5(B[13]), .A6(A[14]), .B6(B[14]), .A7(A[15]), .B7(B[15]), .Less(not_1_out),
    .Bnegate(not_2_out), .Cin(alu_8_1_cout), .Operation({1'b1, not_3_out[0]}), .Cout(alu_8_2_cout),
    .Result0(Result[8]), .Result1(Result[9]), .Result2(Result[10]), .Result3(Result[11]),
    .Result4(Result[12]), .Result5(Result[13]), .Result6(Result[14]), .Result7(Result[15]));  // open: Set, Overflow
  alu_8 alu_8_3 (
    .A0(A[16]), .B0(B[16]), .A1(A[17]), .B1(B[17]), .A2(A[18]), .B2(B[18]), .A3(A[19]), .B3(A[20]),
    .A4(B[19]), .B4(B[20]), .A5(A[21]), .B5(B[21]), .A6(A[22]), .B6(B[22]), .A7(A[23]), .B7(B[23]),
    .Less(not_1_out), .Bnegate(not_2_out), .Cin(alu_8_2_cout), .Operation({1'b1, not_3_out[0]}),
    .Cout(alu_8_3_cout), .Result0(Result[16]), .Result1(Result[17]), .Result2(Result[18]),
    .Result3(Result[19]), .Result4(Result[20]), .Result5(Result[21]), .Result6(Result[22]),
    .Result7(Result[23]));  // open: Set, Overflow
  alu_8 alu_8_4 (
    .A0(A[24]), .B0(B[24]), .A1(A[25]), .B1(B[25]), .A2(A[26]), .B2(B[26]), .A3(A[27]), .B3(B[27]),
    .A4(A[28]), .B4(B[28]), .A5(A[29]), .B5(B[29]), .A6(A[30]), .B6(B[30]), .A7(A[31]), .B7(B[31]),
    .Less(not_1_out), .Bnegate(not_2_out), .Cin(alu_8_3_cout), .Operation({1'b1, not_3_out[0]}),
    .Cout(CarryOut), .Result0(Result[24]), .Result1(Result[25]), .Result2(Result[26]), .Result3(Result[27]),
    .Result4(Result[28]), .Result5(Result[29]), .Result6(Result[30]), .Result7(Result[31]),
    .Set(alu_8_4_set), .Overflow(Overflow));
  nor nor_1 (Equal_Zero, Result[0], Result[1], Result[2], Result[3], Result[4], Result[5], Result[6], Result[7], Result[8], Result[9], Result[10], Result[11], Result[12], Result[13], Result[14], Result[15], Result[16], Result[17], Result[18], Result[19], Result[20], Result[21], Result[22], Result[23], Result[24], Result[25], Result[26], Result[27], Result[28], Result[29], Result[30], Result[31]);
endmodule
