// Logisim project ALU-Control.circ as structural Verilog: 1 circuit, main circuit main
module main (
  input  [1:0] ALUOp,
  input  [5:0] Fucntion,
  output [3:0] ALU_Cntl
);

  wire and_1_out, or_1_out;

  or or_1 (or_1_out, Fucntion[0], Fucntion[3]);
  and and_1 (and_1_out, ALUOp[1], Fucntion[1]);
  and and_2 (ALU_Cntl[0], ALUOp[1], or_1_out);
  or or_2 (ALU_Cntl[2], ALUOp[0], and_1_out);
  or or_3 (ALU_Cntl[1], ~ALUOp[1], ~Fucntion[2]);  // OR_Gate

  assign ALU_Cntl[3] = 1'b0;
endmodule
