// Logisim project Data-Memory.circ as structural Verilog: 1 circuit, main circuit main
module main (
  input  [6:0] Address,
  input  [31:0] Write_Data,
  input  MemWrite,
  input  MemRead,
  input  Clock,
  output [31:0] ReadData
);

  wire not_1_out;

  not not_1 (not_1_out, Clock);
  RAM #(.addrWidth(7), .dataWidth(32), .bus("separate")) ram_1 (
    .addr(Address), .din(Write_Data), .data(ReadData), .str(MemWrite), .clk(not_1_out), .ld(MemRead));  // open: sel, clr
endmodule
