// Logisim project Finale.circ as structural Verilog: 1 circuit, main circuit main
module main (
);

  wire ALU_equal_zero, Clock_out, Main_Control_alusrc, Main_Control_branch, Main_Control_memread,
       Main_Control_memtoreg, Main_Control_memwrite, Main_Control_regdst, Main_Control_regwrite, PCSrc_out;
  wire [1:0] Main_Control_aluop;
  wire [3:0] ALU_Cntl_alu_cntl;
  wire [4:0] multiplexer_1_out, PC_out_2;
  wire [31:0] Add_result, Adder_result, ALU_result, DM_readdata, IM_instruction, multiplexer_2_out,
       multiplexer_3_out, multiplexer_4_out, PC_out, Registers_regdata1, Registers_regdata2,
       Shift_left_output, Sign_Extend__32_bit_result;

  Clock Clock (.out(Clock_out));
  PC_main PC (.In(multiplexer_4_out), .Clock(Clock_out), .Out({PC_out[31:7], PC_out_2, PC_out[1:0]}));
  Instruction_Memory_main IM (.ReadAddr(PC_out_2), .Instruction(IM_instruction));
  alu_32 Add (
    .A(32'h4), .B({PC_out[31:7], PC_out_2, PC_out[1:0]}), .Result(Add_result));  // open: CarryOut, Equal_Zero, Overflow
  Main_Control_main Main_Control (
    .Instruc_31_26(IM_instruction[31:26]), .RegDst(Main_Control_regdst), .ALUSrc(Main_Control_alusrc),
    .MemToReg(Main_Control_memtoreg), .RegWrite(Main_Control_regwrite), .MemRead(Main_Control_memread),
    .MemWrite(Main_Control_memwrite), .Branch(Main_Control_branch), .ALUOp(Main_Control_aluop));
  Multiplexer #(.width(5), .enable("false")) multiplexer_1 (
    .in0(IM_instruction[20:16]), .in1(IM_instruction[15:11]), .out(multiplexer_1_out),
    .sel(Main_Control_regdst));
  sign_extend_main Sign_Extend (.Instruc_15_0(IM_instruction[15:0]), ._32_bit_result(Sign_Extend__32_bit_result));
  _4Reg_32Wide_2Read_1Write Registers (
    .ReadReg1(IM_instruction[22:21]), .ReadReg2(IM_instruction[17:16]), .WriteReg(multiplexer_1_out[1:0]),
    .Clock(Clock_out), .WriteData(multiplexer_2_out), .RegWrite(Main_Control_regwrite),
    .RegData1(Registers_regdata1), .RegData2(Registers_regdata2));
  Multiplexer #(.width(32), .enable("false")) multiplexer_2 (
    .in0(ALU_result), .in1(DM_readdata), .out(multiplexer_2_out), .sel(Main_Control_memtoreg));
  Multiplexer #(.width(32), .enable("false")) multiplexer_3 (
    .in0(Registers_regdata2), .in1(Sign_Extend__32_bit_result), .out(multiplexer_3_out),
    .sel(Main_Control_alusrc));
  shift_left_main Shift_left (.Input(Sign_Extend__32_bit_result), .Output(Shift_left_output));
  alu_32 ALU (
    .A(Registers_regdata1), .B(multiplexer_3_out), .Operation(ALU_Cntl_alu_cntl[2:0]), .Result(ALU_result),
    .Equal_Zero(ALU_equal_zero));  // open: CarryOut, Overflow
  ALU_Control_main ALU_Cntl (.Fucntion(IM_instruction[5:0]), .ALUOp(Main_Control_aluop), .ALU_Cntl(ALU_Cntl_alu_cntl));
  alu_32 Adder (.A(Add_result), .B(Shift_left_output), .Result(Adder_result));  // open: CarryOut, Equal_Zero, Overflow
  Multiplexer #(.width(32), .enable("false")) multiplexer_4 (
    .in0(Add_result), .in1(Adder_result), .out(multiplexer_4_out), .sel(PCSrc_out));
  and PCSrc (PCSrc_out, Main_Control_branch, ALU_equal_zero);
  Data_Memory_main DM (
    .Address(ALU_result[6:0]), .Write_Data(Registers_regdata2), .MemWrite(Main_Control_memwrite),
    .Clock(Clock_out), .MemRead(Main_Control_memread), .ReadData(DM_readdata));
endmodule
