// Logisim project Instruction-Memory.circ as structural Verilog: 1 circuit, main circuit main
module main (
  input  [4:0] ReadAddr,
  output [31:0] Instruction
);

  ROM #(.addrWidth(5), .dataWidth(32)) rom_1 (.addr(ReadAddr), .data(Instruction));  // open: sel
endmodule
