// Logisim project Main-Control.circ as structural Verilog: 1 circuit, main circuit main
module main (
  input  [5:0] Instruc_31_26,
  output RegDst,
  output ALUSrc,
  output MemToReg,
  output RegWrite,
  output MemRead,
  output MemWrite,
  output Branch,
  output [1:0] ALUOp
);

  and and_1 (ALUOp[1], ~Instruc_31_26[5], ~Instruc_31_26[4], ~Instruc_31_26[3], ~Instruc_31_26[2], ~Instruc_31_26[1], ~Instruc_31_26[0]);  // AND_Gate
  and and_2 (MemRead, Instruc_31_26[5], ~Instruc_31_26[4], ~Instruc_31_26[3], ~Instruc_31_26[2], Instruc_31_26[1], Instruc_31_26[0]);  // AND_Gate
  and and_3 (MemWrite, Instruc_31_26[5], ~Instruc_31_26[4], Instruc_31_26[3], ~Instruc_31_26[2], Instruc_31_26[1], Instruc_31_26[0]);  // AND_Gate
  and and_4 (ALUOp[0], ~Instruc_31_26[5], ~Instruc_31_26[4], ~Instruc_31_26[3], Instruc_31_26[2], ~Instruc_31_26[1], ~Instruc_31_26[0]);  // AND_Gate
  or or_1 (ALUSrc, MemRead, MemWrite);
  or or_2 (RegWrite, ALUOp[1], MemRead);

  assign Branch = ALUOp[0];
  assign MemToReg = MemRead;
  assign RegDst = ALUOp[1];
endmodule
