// Logisim project PC.circ as structural Verilog: 1 circuit, main circuit main
module main (
  input  [31:0] In,
  input  Clock,
  output [31:0] Out
);

  Register #(.width(32), .trigger("falling")) PC (.D(In), .Q(Out), .clk(Clock));  // open: en, clr
endmodule
