// Logisim project Registers.circ as structural Verilog: 1 circuit, main circuit 4Reg-32Wide-2Read-1Write
module _4Reg_32Wide_2Read_1Write (
  input  [1:0] ReadReg1,
  input  [1:0] ReadReg2,
  input  [1:0] WriteReg,
  input  Clock,
  input  [31:0] WriteData,
  input  RegWrite,
  output [31:0] RegData1,
  output [31:0] RegData2
);

  wire decoder_1_out0, decoder_1_out1, decoder_1_out2, decoder_1_out3, not_1_out, not_2_out, not_3_out,
       not_4_out, or_1_out, or_2_out, or_3_out, or_4_out;
  wire [31:0] Reg0_q, Reg1_q, Reg2_q, Reg3_q;

  Decoder #(.select(2), .enable("false")) decoder_1 (
    .out0(decoder_1_out0), .out1(decoder_1_out1), .out2(decoder_1_out2), .out3(decoder_1_out3), .sel(WriteReg));
  not not_1 (not_1_out, RegWrite);
  or or_1 (or_1_out, not_1_out, Clock);
  not not_2 (not_2_out, RegWrite);
  or or_2 (or_2_out, not_2_out, Clock);
  not not_3 (not_3_out, RegWrite);
  or or_3 (or_3_out, not_3_out, Clock);
  not not_4 (not_4_out, RegWrite);
  or or_4 (or_4_out, not_4_out, Clock);
  Register #(.width(32), .trigger("falling")) Reg0 (
    .D(WriteData), .en(decoder_1_out0), .Q(Reg0_q), .clk(or_1_out));  // open: clr
  Register #(.width(32), .trigger("falling")) Reg1 (
    .D(WriteData), .en(decoder_1_out1), .Q(Reg1_q), .clk(or_2_out));  // open: clr
  Register #(.width(32), .trigger("falling")) Reg2 (
    .D(WriteData), .en(decoder_1_out2), .Q(Reg2_q), .clk(or_3_out));  // open: clr
  Register #(.width(32), .trigger("falling")) Reg3 (
    .D(WriteData), .en(decoder_1_out3), .Q(Reg3_q), .clk(or_4_out));  // open: clr
  Multiplexer #(.select(2), .width(32), .enable("false")) multiplexer_1 (
    .in0(Reg0_q), .in1(Reg1_q), .in2(Reg2_q), .in3(Reg3_q), .out(RegData1), .sel(ReadReg1));
  Multiplexer #(.select(2), .width(32), .enable("false")) multiplexer_2 (
    .in0(Reg0_q), .in1(Reg1_q), .in2(Reg2_q), .in3(Reg3_q), .out(RegData2), .sel(ReadReg2));
endmodule
