// Logisim project shift-left.circ as structural Verilog: 1 circuit, main circuit main
module main (
  input  [31:0] Input,
  output [31:0] Output
);


  assign Output = {Input[29:0], 2'b00};
endmodule
