// Logisim project sign-extend.circ as structural Verilog: 1 circuit, main circuit main
module main (
  input  [15:0] Instruc_15_0,
  output [31:0] _32_bit_result
);


  assign _32_bit_result = {{17{Instruc_15_0[15]}}, Instruc_15_0[14:0]};
endmodule
